// Logisim project Computadora.circ as structural Verilog: 3 circuits, main circuit Computadora
module Computadora (
  input  ON_OFF
);

  wire bitselector_2_out, button_1_out, clock_1_out, CONTROL_x1, CONTROL_x2, CONTROL_x3, CONTROL_x4,
       CONTROL_x5, CONTROL_x6, CONTROL_x7, CONTROL_x8, CONTROL_x9, CONTROL_x10, CONTROL_x11, CONTROL_x12,
       CONTROL_x13, CONTROL_x14, CONTROL_x15, controlled_buffer_1_out, not_1_out, not_2_out, or_1_out,
       or_2_out, or_3_out, OR_CLEAR_out;
  wire [3:0] bitselector_1_out, CONTROL_counter;
  wire [5:0] bitselector_3_out;
  wire [7:0] A_q, adder_1_out, B_q, COMP_1_out_2, controlled_buffer_2_out, controlled_buffer_3_out,
       counter_1_q, IR_q, MAR_q, MBR_q, multiplexer_1_out, multiplexer_2_out;

  Button button_1 (.out(button_1_out));
  Register #(.trigger("falling")) IR (
    .D(MBR_q), .en(CONTROL_x4), .Q(IR_q), .clk(controlled_buffer_1_out), .clr(button_1_out));
  Counter #(.trigger("falling")) counter_1 (
    .load(CONTROL_x15), .D(MBR_q), .count(CONTROL_x3), .Q(counter_1_q), .clk(controlled_buffer_1_out),
    .clr(button_1_out));  // open: carry
  not not_1 (not_1_out, CONTROL_x1);
  Control CONTROL (
    .IR(bitselector_1_out), .N(bitselector_2_out), .Counter(CONTROL_counter),
    .Clock(controlled_buffer_1_out), .X1(CONTROL_x1), .X2(CONTROL_x2), .X3(CONTROL_x3), .X4(CONTROL_x4),
    .X5(CONTROL_x5), .X6(CONTROL_x6), .X7(CONTROL_x7), .X8(CONTROL_x8), .X9(CONTROL_x9), .X10(CONTROL_x10),
    .X11(CONTROL_x11), .X12(CONTROL_x12), .X13(CONTROL_x13), .X14(CONTROL_x14), .X15(CONTROL_x15),
    .Reset_All(button_1_out));  // open: X16, X17
  BitSelector #(.group(4)) bitselector_1 (.in(IR_q), .out(bitselector_1_out), .sel(1'b0));
  Multiplexer #(.width(8), .enable("false")) multiplexer_1 (
    .in0(counter_1_q), .in1(MBR_q), .out(multiplexer_1_out), .sel(not_1_out));
  Hex_Digit_Display hex_digit_display_1 (.value(CONTROL_counter));  // open: dp
  Register MAR (.D(multiplexer_1_out), .en(or_1_out), .Q(MAR_q), .clk(controlled_buffer_1_out), .clr(button_1_out));
  or or_1 (or_1_out, CONTROL_x1, CONTROL_x6);
  BitSelector bitselector_2 (.in(B_q), .out(bitselector_2_out), .sel(3'b111));
  BitSelector #(.group(6)) bitselector_3 (.in(MAR_q), .out(bitselector_3_out), .sel(1'b0));
  not not_2 (not_2_out, CONTROL_x13);
  or or_2 (or_2_out, CONTROL_x12, CONTROL_x2);
  assign controlled_buffer_1_out = ON_OFF ? clock_1_out : 1'bz;  // Controlled_Buffer controlled_buffer_1
  assign controlled_buffer_2_out = CONTROL_x13 ? MBR_q : 8'bz;  // Controlled_Buffer controlled_buffer_2
  RAM #(.addrWidth(6), .bus("asynch")) ram_1 (
    .addr(bitselector_3_out), .data(controlled_buffer_2_out), .ld(not_2_out), .clr(button_1_out));  // open: sel
  Register #(.trigger("falling")) MBR (
    .D(multiplexer_2_out), .en(or_2_out), .Q(MBR_q), .clk(controlled_buffer_1_out), .clr(button_1_out));
  Clock clock_1 (.out(clock_1_out));
  Multiplexer #(.width(8), .enable("false")) multiplexer_2 (
    .in0(controlled_buffer_2_out), .in1(A_q), .out(multiplexer_2_out), .sel(CONTROL_x12));
  or or_3 (or_3_out, CONTROL_x5, CONTROL_x10, CONTROL_x8);
  Counter #(.trigger("falling")) B (
    .load(or_3_out), .D(controlled_buffer_3_out), .count(CONTROL_x9), .Q(B_q), .clk(controlled_buffer_1_out),
    .clr(button_1_out));  // open: carry
  Counter #(.trigger("falling")) A (
    .load(CONTROL_x7), .D(MBR_q), .count(CONTROL_x14), .Q(A_q), .clk(controlled_buffer_1_out),
    .clr(OR_CLEAR_out));  // open: carry
  or OR_CLEAR (OR_CLEAR_out, button_1_out, CONTROL_x11);
  assign controlled_buffer_3_out = CONTROL_x8 ? COMP_1_out_2 : 8'bz;  // Controlled_Buffer controlled_buffer_3
  COMP1 COMP_1 (.in_1(B_q), .out_2(COMP_1_out_2));
  Adder adder_1 (.a(B_q), .b(A_q), .out(adder_1_out));  // open: cin, cout
  assign controlled_buffer_3_out = CONTROL_x10 ? adder_1_out : 8'bz;  // Controlled_Buffer controlled_buffer_4
  assign controlled_buffer_3_out = CONTROL_x5 ? A_q : 8'bz;  // Controlled_Buffer controlled_buffer_5

  // Notes on the sheet:
  //   RESET_ALL
  //   PC
  //   Tiempo
endmodule

module Control (
  input  [3:0] IR,
  input  N,
  input  Reset_All,
  input  Clock,
  output X1,
  output X2,
  output X3,
  output X4,
  output X5,
  output X6,
  output X7,
  output X8,
  output X9,
  output X10,
  output X11,
  output X12,
  output X13,
  output X14,
  output X15,
  output X16,
  output [3:0] Counter,
  output X17
);

  wire and_1_out, decoder_1_out0, decoder_1_out1, decoder_1_out2, decoder_1_out3, decoder_1_out4,
       decoder_1_out5, decoder_1_out6, decoder_1_out7, decoder_1_out8, decoder_1_out9, decoder_2_out0,
       decoder_2_out1, decoder_2_out2, decoder_2_out3, decoder_2_out4, decoder_2_out5, decoder_2_out6,
       decoder_2_out7, not_1_out, not_2_out, or_1_out, q0t3_out, q1t3_out, q1t4_out, q1t5_out, q1t6_out,
       q1t7_out, q2t3_out, q3t3_out, q4t3_out, q5t3_out, q6t3_out, q6t4_out, q6t5_out, q6t6_out, q6t7_out,
       q7t3_out, q8t3_out, q8t4_out, q8t5_out, q9t3_out, q9t4_out, q9t5N_out, q9t5N_prime_out;

  Counter #(.width(4), .max('hf)) u_Counter (.Q(Counter), .clk(Clock), .clr(or_1_out));  // open: load, D, count, carry
  Decoder #(.select(4)) decoder_1 (
    .out0(decoder_1_out0), .out1(decoder_1_out1), .out2(decoder_1_out2), .out3(decoder_1_out3),
    .out4(decoder_1_out4), .out5(decoder_1_out5), .out6(decoder_1_out6), .out7(decoder_1_out7),
    .out8(decoder_1_out8), .out9(decoder_1_out9), .sel(IR));  // open: out10, out11, out12, out13, out14, out15, en
  Decoder #(.select(4)) decoder_2 (
    .out0(decoder_2_out0), .out1(decoder_2_out1), .out2(decoder_2_out2), .out3(decoder_2_out3),
    .out4(decoder_2_out4), .out5(decoder_2_out5), .out6(decoder_2_out6), .out7(decoder_2_out7), .sel(Counter));  // open: out8, out9, out10, out11, out12, out13, out14, out15, en
  and q0t3 (q0t3_out, decoder_1_out0, decoder_2_out3);
  or or_1 (or_1_out, Reset_All, and_1_out);
  and q1t3 (q1t3_out, decoder_2_out3, decoder_1_out1);
  and q1t4 (q1t4_out, decoder_1_out1, decoder_2_out4);
  and q1t5 (q1t5_out, decoder_1_out1, decoder_2_out5);
  and q1t7 (q1t7_out, decoder_1_out1, decoder_2_out7);
  and q1t6 (q1t6_out, decoder_1_out1, decoder_2_out6);
  and q2t3 (q2t3_out, decoder_1_out2, decoder_2_out3);
  and q3t3 (q3t3_out, decoder_1_out3, decoder_2_out3);
  and q4t3 (q4t3_out, decoder_2_out3, decoder_1_out4);
  and q5t3 (q5t3_out, decoder_1_out5, decoder_2_out3);
  and q6t3 (q6t3_out, decoder_2_out3, decoder_1_out6);
  and q6t4 (q6t4_out, decoder_2_out4, decoder_1_out6);
  and q6t5 (q6t5_out, decoder_2_out5, decoder_1_out6);
  and q6t6 (q6t6_out, decoder_2_out6, decoder_1_out6);
  and q6t7 (q6t7_out, decoder_2_out7, decoder_1_out6);
  and q7t3 (q7t3_out, decoder_2_out3, decoder_1_out7);
  and q8t3 (q8t3_out, decoder_1_out8, decoder_2_out3);
  and q8t4 (q8t4_out, decoder_2_out4, decoder_1_out8);
  and q8t5 (q8t5_out, decoder_2_out5, decoder_1_out8);
  and q9t3 (q9t3_out, decoder_1_out9, decoder_2_out3);
  and q9t4 (q9t4_out, decoder_1_out9, decoder_2_out4);
  and q9t5N (q9t5N_out, decoder_1_out9, decoder_2_out5, N);
  not not_1 (not_1_out, N);
  and q9t5N_prime (q9t5N_prime_out, decoder_1_out9, not_1_out, decoder_2_out5);
  or u_X1 (X1, decoder_2_out0, q1t3_out, q6t3_out, q8t3_out, q9t3_out);
  or u_X2 (X2, decoder_2_out1, q1t4_out, q6t4_out, q8t4_out, q9t4_out, q1t6_out);
  or u_X3 (X3, decoder_2_out1, q1t4_out, q6t4_out, q9t4_out);
  or u_X4 (X4, decoder_2_out2, 1'b0);
  or u_X5 (X5, q0t3_out, 1'b0);
  or u_X6 (X6, q1t5_out, q6t5_out);
  or u_X7 (X7, q1t7_out, 1'b0);
  or u_X8 (X8, q2t3_out, 1'b0);
  or u_X9 (X9, q3t3_out, 1'b0);
  or u_X10 (X10, q4t3_out, 1'b0);
  or u_X11 (X11, q5t3_out, 1'b0);
  or u_X12 (X12, q6t6_out, 1'b0);
  or u_X13 (X13, q6t7_out, 1'b0);
  or u_X14 (X14, q7t3_out, 1'b0);
  or u_X15 (X15, q8t5_out, q9t5N_out);
  or u_X16 (X16, q9t5N_prime_out, 1'b0);
  not not_2 (not_2_out, Clock);
  or u_X17 (X17, X16, X15, X14, X13, X11, X10, X9, X8, X7, X5);
  and and_1 (and_1_out, X17, not_2_out);
endmodule

module COMP1 (
  input  [7:0] in_1,
  output [7:0] out_2
);

  wire [7:0] negator_1_out;

  Negator negator_1 (.in(in_1), .out(negator_1_out));
  Subtractor subtractor_1 (.a(negator_1_out), .b(8'h1), .out(out_2));  // open: bin, bout
endmodule
