// Logisim project Practica1_old.circ as structural Verilog: 3 circuits, main circuit main
module main (
  input  in_1,
  input  in_2
);

  wire button_1_out, button_2_out, button_3_out, clock_1_out, control_1_x1, control_1_x3, control_1_x4,
       control_1_x6, control_1_x15, controlled_buffer_1_out, not_1_out, or_1_out, or_2_out;
  wire [3:0] bitselector_1_out;
  wire [5:0] bitselector_2_out;
  wire [7:0] counter_1_q, IR_q, MAR_q, MBR_q, multiplexer_1_out, ram_1_data;

  Register IR (.D(MBR_q), .en(control_1_x4), .Q(IR_q), .clk(controlled_buffer_1_out));  // open: clr
  Counter counter_1 (.Q(counter_1_q), .clk(or_1_out), .clr(button_1_out));  // open: load, D, count, carry
  Button button_1 (.out(button_1_out));
  or or_1 (or_1_out, control_1_x3, control_1_x15);
  not not_1 (not_1_out, control_1_x1);
  Control control_1 (
    .IR(bitselector_1_out), .N(in_2), .Clock(controlled_buffer_1_out), .X1(control_1_x1), .X3(control_1_x3),
    .X4(control_1_x4), .X6(control_1_x6), .X15(control_1_x15), .Clear(button_2_out));  // open: X2, X5, X7, X8, X9, X10, X11, X12, X13, X14, X16, X17
  BitSelector #(.group(4)) bitselector_1 (.in(IR_q), .out(bitselector_1_out), .sel(1'b0));
  Multiplexer #(.width(8), .enable("false")) multiplexer_1 (
    .in0(counter_1_q), .in1(MBR_q), .out(multiplexer_1_out), .sel(not_1_out));
  Register MAR (.D(multiplexer_1_out), .en(or_2_out), .Q(MAR_q), .clk(controlled_buffer_1_out));  // open: clr
  or or_2 (or_2_out, control_1_x1, control_1_x6);
  Button button_2 (.out(button_2_out));
  BitSelector #(.group(6)) bitselector_2 (.in(MAR_q), .out(bitselector_2_out), .sel(1'b0));
  assign controlled_buffer_1_out = in_1 ? clock_1_out : 1'bz;  // Controlled_Buffer controlled_buffer_1
  Counter counter_2 (.clk(controlled_buffer_1_out), .clr(button_3_out));  // open: load, D, count, Q, carry
  RAM #(.addrWidth(6), .bus("separate")) ram_1 (
    .addr(bitselector_2_out), .din(MBR_q), .data(ram_1_data), .clk(controlled_buffer_1_out));  // open: str, sel, ld, clr
  Register MBR (.D(ram_1_data), .Q(MBR_q), .clk(controlled_buffer_1_out));  // open: en, clr
  Register B ();  // open: D, en, Q, clk, clr
  Clock clock_1 (.out(clock_1_out));
  Button button_3 (.out(button_3_out));
  Register A ();  // open: D, en, Q, clk, clr

  // Notes on the sheet:
  //   PC
endmodule

module Control (
  input  [3:0] IR,
  input  N,
  input  Clear,
  input  Clock,
  output X1,
  output X2,
  output X3,
  output X4,
  output X5,
  output X6,
  output X7,
  output X8,
  output X9,
  output X10,
  output X11,
  output X12,
  output X13,
  output X14,
  output X15,
  output X16,
  output X17
);

  wire decoder_1_out0, decoder_1_out1, decoder_1_out2, decoder_1_out3, decoder_1_out4, decoder_1_out5,
       decoder_1_out6, decoder_1_out7, decoder_1_out8, decoder_1_out9, decoder_2_out0, decoder_2_out1,
       decoder_2_out2, decoder_2_out3, decoder_2_out4, decoder_2_out5, decoder_2_out6, decoder_2_out7,
       not_1_out, q0t3_out, q1t3_out, q1t4_out, q1t5_out, q1t7_out, q2t3_out, q3t3_out, q4t3_out, q5t3_out,
       q6t3_out, q6t4_out, q6t5_out, q6t6_out, q6t7_out, q7t3_out, q8t3_out, q8t4_out, q8t5_out, q9t3_out,
       q9t4_out, q9t5N_out;
  wire [3:0] Counter_q;

  Counter #(.width(4), .max('hf)) Counter (.Q(Counter_q), .clk(Clock), .clr(Clear));  // open: load, D, count, carry
  Decoder #(.select(4)) decoder_1 (
    .out0(decoder_1_out0), .out1(decoder_1_out1), .out2(decoder_1_out2), .out3(decoder_1_out3),
    .out4(decoder_1_out4), .out5(decoder_1_out5), .out6(decoder_1_out6), .out7(decoder_1_out7),
    .out8(decoder_1_out8), .out9(decoder_1_out9), .sel(IR));  // open: out10, out11, out12, out13, out14, out15, en
  Decoder #(.select(4)) decoder_2 (
    .out0(decoder_2_out0), .out1(decoder_2_out1), .out2(decoder_2_out2), .out3(decoder_2_out3),
    .out4(decoder_2_out4), .out5(decoder_2_out5), .out6(decoder_2_out6), .out7(decoder_2_out7),
    .sel(Counter_q));  // open: out8, out9, out10, out11, out12, out13, out14, out15, en
  and q0t3 (q0t3_out, decoder_1_out0, decoder_2_out3);
  and q1t3 (q1t3_out, decoder_2_out3, decoder_1_out1);
  and q1t4 (q1t4_out, decoder_1_out1, decoder_2_out4);
  and q1t5 (q1t5_out, decoder_1_out1, decoder_2_out5);
  and q1t7 (q1t7_out, decoder_1_out1, decoder_2_out7);
  and q2t3 (q2t3_out, decoder_1_out2, decoder_2_out3);
  and q3t3 (q3t3_out, decoder_1_out3, decoder_2_out3);
  and q4t3 (q4t3_out, decoder_2_out3, decoder_1_out4);
  and q5t3 (q5t3_out, decoder_1_out5, decoder_2_out3);
  and q6t3 (q6t3_out, decoder_2_out3, decoder_1_out6);
  and q6t4 (q6t4_out, decoder_2_out4, decoder_1_out6);
  and q6t5 (q6t5_out, decoder_2_out5, decoder_1_out6);
  and q6t6 (q6t6_out, decoder_2_out6, decoder_1_out6);
  and q6t7 (q6t7_out, decoder_2_out7, decoder_1_out6);
  and q7t3 (q7t3_out, decoder_2_out3, decoder_1_out7);
  and q8t3 (q8t3_out, decoder_1_out8, decoder_2_out3);
  and q8t4 (q8t4_out, decoder_2_out4, decoder_1_out8);
  and q8t5 (q8t5_out, decoder_2_out5, decoder_1_out8);
  and q9t3 (q9t3_out, decoder_1_out9, decoder_2_out3);
  and q9t4 (q9t4_out, decoder_1_out9, decoder_2_out4);
  and q9t5N (q9t5N_out, decoder_1_out9, decoder_2_out5, N);
  not not_1 (not_1_out, N);
  or u_X1 (X1, decoder_2_out0, q1t3_out, q6t3_out, q8t3_out, q9t3_out);
  or u_X2 (X2, decoder_2_out1, q1t4_out, q6t4_out, q8t4_out, q9t4_out);
  or u_X3 (X3, decoder_2_out1, q1t4_out, q6t4_out, q9t4_out);
  or u_X4 (X4, decoder_2_out2, 1'b0);
  or u_X5 (X5, q0t3_out, 1'b0);
  or u_X6 (X6, q1t5_out, q6t5_out);
  or u_X7 (X7, q1t7_out, 1'b0);
  or u_X8 (X8, q2t3_out, 1'b0);
  or u_X9 (X9, q3t3_out, 1'b0);
  or u_X10 (X10, q4t3_out, 1'b0);
  or u_X11 (X11, q5t3_out, 1'b0);
  or u_X12 (X12, q6t6_out, 1'b0);
  or u_X13 (X13, q6t7_out, 1'b0);
  or u_X14 (X14, q7t3_out, 1'b0);
  or u_X15 (X15, q8t5_out, q9t5N_out);
  or u_X16 (X16, not_1_out, 1'b0);
  or u_X17 (X17, X16, X15, X14, X12, X11, X10, X9, X8, X7, X5);
endmodule

module SBP (
  input  [3:0] in_1,
  output [3:0] out_2
);

  wire [3:0] negator_1_out;

  Negator #(.width(4)) negator_1 (.in(in_1), .out(negator_1_out));
  Subtractor #(.width(4)) subtractor_1 (.a(negator_1_out), .b(4'b0001), .out(out_2));  // open: bin, bout
endmodule
